# Fritzing sketch esp8266_sensors (saved by Fritzing 0.9.3b)
circuit board: 4.99706cm x 4.98238cm
perfboards: 1

parts:
  IC1 = Voltage Regulator [package=to-92]
  S2 = Pushbutton [package="[THT]"]
  J5 = male pin header, 2 pins [form="♂ (male)"]
  J4 = female pin header, 6 pins [form="♀ (female)"]
  R2 = Resistor [tolerance=±5% resistance=10k package=THT]
  R3 = Resistor [tolerance=±5% resistance=10k package=THT]
  J10 = Screw terminal - 2 pins [package=THT]
  R4 = Resistor [tolerance=±5% resistance=330k package=THT]
  J11 = male pin header, 2 pins [form="♂ (male)"]
  C1 = Tantalum Capacitor [capacitance=2.2µF package="100 mil [THT, tantalum]"]
  C2 = Tantalum Capacitor [capacitance=2.2µF package="100 mil [THT, tantalum]"]
  U5 = mystery part, 6 pins [chip_label=?]
  U6 = mystery part, 6 pins [chip_label=?]
  U7 = mystery part, 6 pins [chip_label=?]
  DHT1 = DHT22_Humidity_and_Temperature_Sensor
  Q1 = Basic FET N-Channel [package="TO220 [THT]"]
  R6 = Resistor [tolerance=±5% resistance=100k package=THT]
  J12 = female pin header, 11 pins [form="♀ (female)"]
  J13 = female pin header, 2 pins [form="♀ (female)"]
  U11 = mystery part, 6 pins [chip_label=?]
  U12 = mystery part, 6 pins [chip_label=?]
  R1 = Resistor [tolerance=±5% resistance=10k package=THT]
  R5 = Resistor [tolerance=±5% resistance=47k package=THT]
  MOD-WIFI-ESP8266-DEV1 = OLIMEX_MOD-WIFI-ESP8266-DEV
  U10 = mystery part, 9 pins [chip_label=?]
  U9 = mystery part, 9 pins [chip_label=?]
  U8 = mystery part, 9 pins [chip_label=?]

nets:
  GND: IC1.GND, S2.Pin_1, S2.Pin_2, J4.pin1, J10.pin1, C1.-, C2.-, DHT1.connector4, Q1.source, R6.Pin_0, J12.pin10, R5.Pin_0, MOD-WIFI-ESP8266-DEV1.connector1
  N1: IC1.IN, J10.pin2, R4.Pin_0, C2.+
  3V3: IC1.OUT, R2.Pin_0, R3.Pin_0, C1.+, DHT1.connector1, J12.pin11, R1.Pin_1, MOD-WIFI-ESP8266-DEV1.connector0
  RSTB: S2.Pin_3, S2.Pin_4, J5.pin2, MOD-WIFI-ESP8266-DEV1.connector13
  GPIO16: J5.pin1, MOD-WIFI-ESP8266-DEV1.connector15
  GPIO3: J4.pin4, MOD-WIFI-ESP8266-DEV1.connector3
  GPIO1: J4.pin5, MOD-WIFI-ESP8266-DEV1.connector2
  GPIO4: R2.Pin_1, J12.pin7, MOD-WIFI-ESP8266-DEV1.connector22
  GPIO5: R3.Pin_1, J12.pin8, MOD-WIFI-ESP8266-DEV1.connector11
  N2: R4.Pin_1, J11.pin1, R5.Pin_1
  ADC: J11.pin2, MOD-WIFI-ESP8266-DEV1.connector12
  N3: U5.pin1, U5.pin2, U5.pin3
  N4: U5.pin4, U5.pin5, U5.pin6
  N5: U6.pin1, U6.pin2, U6.pin3
  N6: U6.pin4, U6.pin5, U6.pin6
  N7: U7.pin1, U7.pin2, U7.pin3
  N8: U7.pin4, U7.pin5, U7.pin6
  GPIO13: DHT1.connector2, J12.pin3, R1.Pin_0, MOD-WIFI-ESP8266-DEV1.connector18
  N9: Q1.gate, R6.Pin_1, J13.pin2
  GNDSW: Q1.drain, J12.pin9
  GPIO12: J12.pin1, MOD-WIFI-ESP8266-DEV1.connector16
  GPIO14: J12.pin2, MOD-WIFI-ESP8266-DEV1.connector17
  GPIO15: J12.pin4, J13.pin1, MOD-WIFI-ESP8266-DEV1.connector19
  GPIO2: J12.pin5, MOD-WIFI-ESP8266-DEV1.connector20
  GPIO0: J12.pin6, MOD-WIFI-ESP8266-DEV1.connector21
  N10: U11.pin1, U11.pin2, U11.pin3
  N11: U11.pin4, U11.pin5, U11.pin6
  N12: U12.pin1, U12.pin2, U12.pin3
  N13: U12.pin4, U12.pin5, U12.pin6
  N14: U10.pin1, U10.pin2, U10.pin3
  N15: U10.pin4, U10.pin5, U10.pin6
  N16: U10.pin7, U10.pin8, U10.pin9
  N17: U9.pin1, U9.pin2, U9.pin3
  N18: U9.pin4, U9.pin5, U9.pin6
  N19: U9.pin7, U9.pin8, U9.pin9
  N20: U8.pin1, U8.pin2, U8.pin3
  N21: U8.pin4, U8.pin5, U8.pin6
  N22: U8.pin7, U8.pin8, U8.pin9

notes:
  GND
  CTS
  POWER
  TXO
  RXI
  DTR
  GPIO1: U0TXD -> RXI
  GPIO3: U0RXD -> TXO
  RESET
  IC1: MCP1700-3302E/TO
  C1 and C2: 2.2µF
  Prototype Area
  I2C: GPIO4/22 -> SDA, GPIO5/11 -> SCL
  Bridge J11 to measure bat voltage
